// Logisim project digitalDisplay.circ as structural Verilog: 1 circuit, main circuit main
module main (
  input  in_1,
  input  in_2,
  input  [3:0] in_3
);

  wire _0, _1, _2, _3, _4, _5, _6, _7, _8, _9, bl, bot, br, dot, mid, tl, top, tr;

  Demultiplexer #(.select(4), .disabled(0)) demultiplexer_1 (
    .out0(_0), .out1(_1), .out2(_2), .out3(_3), .out4(_4), .out5(_5), .out6(_6), .out7(_7), .out8(_8),
    .out9(_9), .in(in_1), .sel(in_3), .en(in_2));  // open: out10, out11, out12, out13, out14, out15
  xnor u__6 (tr, _6, _5);
  NotExactlyOne xnor_1 (.out(mid), .in0(_0), .in1(_1), .in2(_7));
  NotExactlyOne xnor_2 (.out(tl), .in0(_1), .in1(_2), .in2(_3), .in3(_7));
  NotExactlyOne xnor_3 (.out(bot), .in0(_1), .in1(_4), .in2(_7));
  xnor xnor_4 (top, _4, _1);
  not not_1 (br, _2);
  _7_Segment_Display u_7_segment_display_1 (.g(mid), .f(tl), .a(top), .b(tr), .e(bl), .d(bot), .c(br), .dp(dot));
  NotExactlyOne xnor_5 (.out(bl), .in0(_3), .in1(_1), .in2(_4), .in3(_9), .in4(_7), .in5(_5));
endmodule
